# Fritzing sketch kl25z-bike-computer-schematic-0.1 (saved by Fritzing 0.9.0b)
breadboards: 1

parts:
  S1 = Reed switch [package=THT]
  R1 = Resistor [tolerance=±5% resistance=350 package=THT]

nets:
  5V: S1.pin_1
  D5: S1.pin_2, R1.Pin_0
